# Fritzing sketch CatanDice (saved by Fritzing 0.9.6b)
perfboards: 1

parts:
  LCD1 = TFT 1.8 inch 160x128 w SD
  SW = ENCODER_AB [package=encoder_led_3]
  C1 = Capacitor [package=cap-pth-large]
  R1 = Resistor [tolerance=±5% power=0.25 resistance=10k package=THT]
  R2 = Resistor [tolerance=±5% power=0.25 resistance=10k package=THT]
  R3 = Resistor [tolerance=±5% power=0.25 resistance=10k package=THT]
  C2 = Capacitor [package=cap-pth-large]
  C3 = Capacitor [package=cap-pth-large]
  Q1 = TRANSISTOR_NPN [package=to-92]
  R4 = Resistor [tolerance=±5% power=0.25 resistance=10k package=THT]
  Mod1 = Raspberry Pi Pico
  J1 = Piezo Speaker

nets:
  N1: LCD1.pin_1, Mod1.pin_14
  N2: LCD1.pin_2, Mod1.pin_7
  N3: LCD1.pin_3, Mod1.pin_15
  N4: LCD1.pin_4, Mod1.pin_5
  N5: LCD1.pin_5, Mod1.pin_4
  N6: LCD1.pin_6, Mod1.pin_36
  N7: LCD1.pin_7, Mod1.pin_17
  N8: LCD1.pin_8, Mod1.pin_3, Mod1.pin_8, Mod1.pin_13, Mod1.pin_18, Mod1.pin_23, Mod1.pin_28, Mod1.pin_33, Mod1.pin_38
  N9: LCD1.pin_9, Mod1.pin_24
  N10: LCD1.pin_10, Mod1.pin_21
  N11: LCD1.pin_11, Mod1.pin_25
  N12: LCD1.pin_12, Mod1.pin_22
  N13: SW.P1, SW.G, C1.2, C2.2, C3.2, Q1.E
  N14: SW.P2, R1.Pin_1
  N15: SW.A, R3.Pin_1
  N16: SW.B, R2.Pin_1
  N17: C1.1, R1.Pin_0, Mod1.pin_10
  N18: R2.Pin_0, C3.1, Mod1.pin_12
  N19: R3.Pin_0, C2.1, Mod1.pin_11
  N20: Q1.B, R4.Pin_1
  N21: Q1.C, J1.pin2
  N22: R4.Pin_0, Mod1.pin_9
  N23: Mod1.pin_40, J1.pin1

custom parts:
  TFT 1.8 inch 160x128 w SD: This is a generic 1.8 tft spi lcd display available on ebay and others. The 1.8" display has 128x160 color pixels china version
  ENCODER_AB: Rotary Encoder and select switch EC12PLRGBSDVBF-D: http://top-up.so-buy.com/front/bin/ptdetail.phtml?Part=EC12PLRGBSDVBF-D
  Raspberry Pi Pico: Raspberry Pi Pico. Based around the RP2040 microcontroller the Pico is a low cost microcontroller device bringing Raspberry Pi quality, cost, and easy of use to the microcontroller space. Jan 2021, Split part in to two versions: tht (this one) and SMD. This one will drill holes for a .1 in header in pcb to allow plugging in the module as well as providing pads to solder the module to the top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
